# Fritzing sketch rc-car-lights (saved by Fritzing 1.0.4)
breadboards: 2

parts:
  U1 = 74HC595 [package="DIP16 [THT]"]
  Part1 = Arduino Uno (Rev3) - ICSP
  ResBeam = Resistor [tolerance=±5% power=0.25W resistance=220 package=THT]
  HeadLeft = LED - 5mm [color="White (4500K)" current=0.030A package="5 mm [THT]"]
  RTurnLeft = Resistor [tolerance=±5% power=0.25W resistance=220 package=THT]
  TurnFrontLeft1 = LED - 3mm [color="Yellow (595nm)" current=0.030A package="3 mm [THT]"]
  PinHeaderSatelliteFrontLeft1 = female pin header, 3 pins [form="♀ (female)"]
  ResDay = Resistor [tolerance=±5% power=0.25W resistance=220 package=THT]
  PinHeaderMainFrontLeft1 = female pin header, 3 pins [form="♀ (female)"]
  PinHeaderMainFrontLeft2 = female pin header, 3 pins [form="♀ (female)"]
  JMainFrontRight1 = female pin header, 3 pins [form="♀ (female)"]
  JFrontRight2 = female pin header, 3 pins [form="♀ (female)"]
  RTurnRight = Resistor [tolerance=±5% power=0.25W resistance=220 package=THT]
  RReverse = Resistor [tolerance=±5% power=0.25W resistance=220 package=THT]
  RTail = Resistor [tolerance=±5% power=0.25W resistance=220 package=THT]
  RBrake = Resistor [tolerance=±5% power=0.25W resistance=220 package=THT]
  JMainBackLeft = female pin header, 5 pins [form="♀ (female)"]

nets:
  N1: U1.Q1, RTurnLeft.Pin_1
  N2: U1.Q2, ResBeam.Pin_1
  N3: U1.Q3, ResDay.Pin_1
  N4: U1.Q4, RTail.Pin_1
  N5: U1.Q5, RBrake.Pin_1
  N6: U1.Q6, RReverse.Pin_1
  N7: U1.GND, RTurnRight.Pin_1
  N8: U1.MR, U1.VCC
  N9: U1.SH_CP, Part1.D9_PWM
  N10: U1.ST_CP, Part1.D11_PWM/MOSI
  GND: U1.OE, HeadLeft.cathode, TurnFrontLeft1.cathode, PinHeaderSatelliteFrontLeft1.pin1, PinHeaderMainFrontLeft1.pin1, PinHeaderMainFrontLeft2.pin1, JMainFrontRight1.pin1, JFrontRight2.pin1, JMainBackLeft.pin1
  N11: U1.DS, Part1.D12/MISO
  N12: ResBeam.Pin_0, HeadLeft.anode, PinHeaderSatelliteFrontLeft1.pin3, PinHeaderMainFrontLeft1.pin3, JMainFrontRight1.pin3
  N13: RTurnLeft.Pin_0, TurnFrontLeft1.anode, PinHeaderSatelliteFrontLeft1.pin2, PinHeaderMainFrontLeft1.pin2, PinHeaderMainFrontLeft2.pin2
  N14: ResDay.Pin_0, PinHeaderMainFrontLeft2.pin3, JFrontRight2.pin3
  N15: JMainFrontRight1.pin2, JFrontRight2.pin2, RTurnRight.Pin_0, JMainBackLeft.pin2
  N16: RReverse.Pin_0, JMainBackLeft.pin5
  N17: RTail.Pin_0, JMainBackLeft.pin3
  N18: RBrake.Pin_0, JMainBackLeft.pin4
